// Logisim project logisim_202404240949.circ as structural Verilog: 1 circuit, main circuit main
module main (
  input  LOCK,
  input  DIN,
  output DOUT,
  output out_4
);

  wire and_1_out, and_2_out, not_1_out, not_2_out;

  not not_1 (not_1_out, DIN);
  not not_2 (not_2_out, LOCK);
  and and_1 (and_1_out, not_1_out, not_2_out);
  and and_2 (and_2_out, not_2_out, DIN);
  nor nor_1 (DOUT, and_1_out, out_4);
  nor nor_2 (out_4, DOUT, and_2_out);
endmodule
