// Logisim project logisim_202404241004.circ as structural Verilog: 1 circuit, main circuit main
module main (
  input  LOCK,
  input  DIN,
  output DOUT_1,
  output out_4,
  output DOUT_2,
  output out_6
);

  wire and_1_out, and_2_out, and_3_out, and_4_out, not_1_out, not_2_out;

  not not_1 (not_1_out, DIN);
  not not_2 (not_2_out, LOCK);
  and and_1 (and_1_out, not_1_out, not_2_out);
  and and_2 (and_2_out, not_2_out, DIN);
  nor nor_1 (DOUT_1, and_1_out, out_6);
  nor nor_2 (out_6, DOUT_1, and_2_out);
  and and_3 (and_3_out, DOUT_1, LOCK);
  and and_4 (and_4_out, LOCK, out_6);
  nor nor_3 (out_4, and_3_out, DOUT_2);
  nor nor_4 (DOUT_2, out_4, and_4_out);
endmodule
