// Logisim project logisim_202404241050.circ as structural Verilog: 1 circuit, main circuit main
module main (
  input  R_reset,
  input  S_din,
  output Q_dout,
  output out_4
);

  nor nor_1 (Q_dout, R_reset, out_4);
  nor nor_2 (out_4, Q_dout, S_din);
endmodule
